# Fritzing sketch LED switch circuit (saved by Fritzing 0.8.5b)
breadboards: 1

parts:
  R1 = Resistor [tolerance=±5% resistance=100k package=THT]
  Part1 = Arduino Uno (Rev3)
  LED1 = smd LED [color="Yellow (595nm)" package="0603 [SMD]"]

nets:
  N1: R1.Pin_0, Part1.GND, LED1.cathode
  N2: R1.Pin_1, Part1.D2
  N3: Part1.D13/SCK, LED1.anode
