# Fritzing sketch Input - Distance (saved by Fritzing 0.9.1b)
breadboards: 1

parts:
  Part2 = SRF05 Ultrasonic Rangefinder
  Part3 = Arduino Uno (Rev3)
  C1 = Ceramic Capacitor [capacitance="100 nF" package="0603 [SMD, multilayer]"]
  R1 = Resistor [package="2512 [SMD]"]

nets:
  VCC: Part2.VCC, Part3.5V
  N1: Part2.Trig, Part3.D13/SCK
  N2: Part2.Echo, Part3.D12/MISO
  GND: Part2.GND, Part3.GND, C1.1
  N3: Part3.D3_PWM, R1.Pin_0
  N4: C1.0, R1.Pin_1
