# Fritzing sketch Input - LDR (saved by Fritzing 0.9.1b)
breadboards: 1

parts:
  R1 = Photocell (LDR) [package=THT]
  R2 = Resistor [tolerance=±5% resistance=1k package="0805 [SMD]"]

nets:
  N1: R1.pin_1, R2.Pin_0
