# Fritzing sketch LDRtoServo (saved by Fritzing 0.9.1b)
breadboards: 2

parts:
  Part1 = Intel Galileo Gen2
  J1 = Basic Servo
  R3 = Photocell (LDR) [package=THT]
  R4 = Resistor [tolerance=±5% resistance=1k package="0805 [SMD]"]

nets:
  N1: Part1.A0, R3.pin_1, R4.Pin_0
  N2: Part1.D11_PWM/MOSI, J1.pulse
  5V: Part1.5V, J1.vcc, R4.Pin_1
  GND: Part1.GND, J1.gnd, R3.pin_0
