# Fritzing sketch Output - LED ring - OneInput (saved by Fritzing 0.9.1b)
breadboards: 1

parts:
  neopixel1 = Neopixel 24 Ring
  Part2 = Arduino Uno (Rev3)
  C1 = Capacitor [package=cap-pth-small-kit]
  R3 = Resistor [tolerance=±5% resistance=220 package="0603 [SMD]"]

nets:
  GND: neopixel1.GND, Part2.A1, Part2.GND, C1.2
  VCC: neopixel1.Vcc, Part2.5V
  N1: neopixel1.IN, Part2.D6_PWM
  N2: Part2.A0, C1.1, R3.Pin_1
