# Fritzing sketch Output - LED ring (saved by Fritzing 0.9.1b)
breadboards: 1

parts:
  Part1 = Arduino Nano (Rev3.0)
  neopixel1 = Neopixel 24 Ring

nets:
  GND: Part1.GND, neopixel1.GND
  N1: Part1.D6, neopixel1.IN
  5V: Part1.5V, neopixel1.Vcc
