# Fritzing sketch Output - LED (saved by Fritzing 0.8.5b)
breadboards: 1

parts:
  R1 = Resistor [tolerance=±5% resistance=220 package="0805 [SMD]"]
  LED1 = smd LED [color="Red (633nm)" package="0805 [SMD]"]

nets:
  N1: R1.Pin_1, LED1.cathode
